# Fritzing sketch basic_connection (saved by Fritzing 0.9.3b)

parts:
  Raspberry_Pi1 = Raspberry Pi 2
  LPD8806_RGB_LED_Strip2 = LPD8806 RGB LED Strip

nets:
  N1: Raspberry_Pi1.GPIO10, LPD8806_RGB_LED_Strip2.DI
  N2: Raspberry_Pi1.GPIO11, LPD8806_RGB_LED_Strip2.CI
  GND: Raspberry_Pi1.GND, LPD8806_RGB_LED_Strip2.GND
  5V: Raspberry_Pi1.5V, LPD8806_RGB_LED_Strip2.+5V

custom parts:
  LPD8806 RGB LED Strip: Digitally addressable RGB LED strip
